// Digital circuit BeanBoardSPI.dig as structural Verilog
module BeanBoardSPI (
  input  SER_WRITE,
  input  DO0,
  input  DO1,
  input  DO2,
  input  DO3,
  input  DO4,
  input  DO5,
  input  DO6,
  input  DO7,
  input  CLK,
  input  enable,
  input  SER_IN,
  input  CTRL_WRITE,
  input  D0,
  input  D1,
  input  D2,
  input  D3,
  input  D4,
  input  D5,
  input  D6,
  input  D7,
  input  RD,
  input  WR,
  input  IORQ,
  input  A1,
  input  A2,
  input  A3,
  output SER_OUT,
  output CS0,
  output SCK,
  output DI0,
  output DI1,
  output DI2,
  output DI3,
  output DI4,
  output DI5,
  output DI6,
  output DI7,
  output CS1,
  output CS2,
  output CS3,
  output CS4,
  output CS5,
  output CS6,
  output SRESET,
  output D0_2,
  output D1_2,
  output D2_2,
  output D3_2,
  output D4_2,
  output D5_2,
  output D6_2,
  output D7_2
);

  wire _74165_1_pin9, _74165_1_pin10, _74165_3_pin10, clk_t, clk_t_t, ctrl_latch, swr_t;

  assign D0_2 = ~WR ? D0 : 1'bz;  // DriverInvSel driverinvsel_1
  assign D1_2 = ~WR ? D1 : 1'bz;  // DriverInvSel driverinvsel_2
  assign D2_2 = ~WR ? D2 : 1'bz;  // DriverInvSel driverinvsel_3
  assign D3_2 = ~WR ? D3 : 1'bz;  // DriverInvSel driverinvsel_4
  assign D4_2 = ~WR ? D4 : 1'bz;  // DriverInvSel driverinvsel_5
  assign D5_2 = ~WR ? D5 : 1'bz;  // DriverInvSel driverinvsel_6
  assign D6_2 = ~WR ? D6 : 1'bz;  // DriverInvSel driverinvsel_7
  assign D7_2 = ~WR ? D7 : 1'bz;  // DriverInvSel driverinvsel_8
  and and_1 (clk_t_t, CLK, enable);
  not not_1 (swr_t, SER_WRITE);
  not not_2 (ctrl_latch, CTRL_WRITE);
  not not_3 (clk_t, clk_t_t);
  // ScopeTrigger scopetrigger_1: pin names not known; wires that end beside it: clk_t_t
  _74165 _74165_1 (
    .pin1(SER_WRITE), .pin2(clk_t_t), .pin3(1'b1), .pin4(1'b1), .pin5(1'b1), .pin6(1'b0), .pin8(1'b0),
    .pin9(_74165_1_pin9), .pin10(_74165_1_pin10), .pin11(1'b1), .pin12(1'b1), .pin13(1'b1), .pin14(1'b1),
    .pin15(swr_t), .pin16(1'b1));  // open: pin7
  _74165 _74165_2 (
    .pin1(SER_WRITE), .pin2(clk_t_t), .pin3(1'b0), .pin4(1'b0), .pin5(1'b0), .pin6(1'b1), .pin8(1'b0),
    .pin9(_74165_1_pin10), .pin10(1'b0), .pin11(1'b0), .pin12(1'b0), .pin13(1'b0), .pin14(1'b0),
    .pin15(swr_t), .pin16(1'b1));  // open: pin7
  _74165 _74165_3 (
    .pin1(SER_WRITE), .pin2(clk_t_t), .pin3(DO5), .pin4(DO6), .pin5(DO7), .pin6(1'b0), .pin8(1'b0),
    .pin9(SER_OUT), .pin10(_74165_3_pin10), .pin11(DO1), .pin12(DO2), .pin13(DO3), .pin14(DO4),
    .pin15(swr_t), .pin16(1'b1));  // open: pin7
  _74165 _74165_4 (
    .pin1(SER_WRITE), .pin2(clk_t_t), .pin3(1'b0), .pin4(1'b0), .pin5(1'b0), .pin6(DO0), .pin8(1'b0),
    .pin9(_74165_3_pin10), .pin10(1'b0), .pin11(1'b0), .pin12(1'b0), .pin13(1'b0), .pin14(1'b0),
    .pin15(swr_t), .pin16(1'b1));  // open: pin7
  _74164 _74164_1 (
    .pin1(SER_IN), .pin2(_74165_1_pin9), .pin3(DI0), .pin4(DI1), .pin5(DI2), .pin6(DI3), .pin7(1'b0),
    .pin8(SCK), .pin9(SER_WRITE), .pin10(DI4), .pin11(DI5), .pin12(DI6), .pin13(DI7), .pin14(1'b1));
  and and_2 (SCK, _74165_1_pin9, clk_t);
  _74373 _74373_1 (
    .pin1(1'b0), .pin2(SRESET), .pin3(D0_2), .pin4(D1_2), .pin5(CS0), .pin6(CS1), .pin7(D2_2), .pin8(D3_2),
    .pin9(CS2), .pin10(1'b0), .pin11(ctrl_latch), .pin12(CS3), .pin13(D4_2), .pin14(D5_2), .pin15(CS4),
    .pin16(CS5), .pin17(D6_2), .pin18(D7_2), .pin19(CS6), .pin20(1'b1));

  // Other names for the same wires on the sheet: cs_0 = CS0; cs_1 = CS1; cs_2 = CS2; cs_3 = CS3; cs_4 = CS4;
  //   cs_5 = CS5; cs_6 = CS6; d0_t = D0_2; d1_t = D1_2; d2_t = D2_2; d3_t = D3_2; d4_t = D4_2; d5_t = D5_2;
  //   d6_t = D6_2; d7_t = D7_2; sclk = SCK; swr = SER_WRITE

  // Notes on the sheet:
  //   SER_WRITE: default 1
  //   enable: default 1
  //   SER_IN: default 1
  //   CTRL_WRITE: default 1
  //   D0: default 1
  //   D1: default 1
  //   D2: default 1
  //   D3: default 1
  //   D4: default 1
  //   D5: default 1
  //   D6: default 1
  //   D7: default 1
  //   RD: default 1
  //   WR: default 1
  //   IORQ: default 1
  //   A3: default 1
  //   Z80
  //   SPI
  //   Ctrl
  //   Bits
  //   reset
  //   cs0
  //   cs1
  //   cs2
  //   cs3
  //   cs4
  //   cs5
  //   cs6
  //   Counter
  //   Serial Out
  //   Serial In
  //   SPI Control Register
endmodule
